# Fritzing sketch lcd hex ascii (saved by Fritzing 1.0.3b)
breadboards: 2

parts:
  S1 = Pushbutton [package="[THT]"]
  S2 = Pushbutton [package="[THT]"]
  S3 = Pushbutton [package="[THT]"]
  S4 = Pushbutton [package="[THT]"]
  R1 = Resistor [tolerance=±5% resistance=220 package="0805 [SMD]"]
  U2 = POT [knob_status=50% power=0.5W package=alps_pot]
  R2 = Resistor [tolerance=±5% resistance=220 package="0805 [SMD]"]
  R3 = Resistor [tolerance=±5% resistance=220 package="0805 [SMD]"]
  R4 = Resistor [tolerance=±5% resistance=220 package="0805 [SMD]"]
  R5 = Resistor [tolerance=±5% resistance=220 package="0805 [SMD]"]
  R9 = Resistor [tolerance=±5% resistance=220 package="0805 [SMD]"]  # not connected
  R12 = Resistor [tolerance=±5% resistance=220 package="0805 [SMD]"]
  U4 = LCD-16X2 [package=lcd-16x2_noholes]
  DI1 = 7-Segment LED Display [package=THT]
  R13 = Resistor [tolerance=±5% resistance=220 package="0805 [SMD]"]
  R14 = Resistor [tolerance=±5% resistance=220 package="0805 [SMD]"]
  R15 = Resistor [tolerance=±5% resistance=220 package="0805 [SMD]"]
  R16 = Resistor [tolerance=±5% resistance=220 package="0805 [SMD]"]
  DI2 = 7-Segment LED Display [package=THT]  # not connected
  part = TTP223B Capacitive Touch Sensor Module [part_number="Touch sensor"]
  part_2 = TTP223B Capacitive Touch Sensor Module [part_number="Touch sensor"]
  part_3 = TTP223B Capacitive Touch Sensor Module [part_number="Touch sensor"]
  R17 = Resistor [tolerance=±5% resistance=220 package="0805 [SMD]"]
  R19 = Resistor [tolerance=±5% resistance=220 package="0805 [SMD]"]
  U1 = Carte NUCLEO H755ZI-Q
  R18 = Resistor [tolerance=±5% resistance=220 package="0805 [SMD]"]
  R20 = Resistor [tolerance=±5% resistance=220 package="0805 [SMD]"]
  R21 = Resistor [tolerance=±5% resistance=220 package="0805 [SMD]"]
  R22 = Resistor [tolerance=±5% resistance=220 package="0805 [SMD]"]
  R23 = Resistor [tolerance=±5% resistance=220 package="0805 [SMD]"]
  R24 = Resistor [tolerance=±5% resistance=220 package="0805 [SMD]"]
  R25 = Resistor [tolerance=±5% resistance=220 package="0805 [SMD]"]
  R8 = Resistor [tolerance=±5% resistance=220 package="0805 [SMD]"]

nets:
  N1: S1.Pin_1, S1.Pin_2, S2.Pin_1, S2.Pin_2, S3.Pin_1, S3.Pin_2, S4.Pin_1, S4.Pin_2
  N2: S1.Pin_3, S1.Pin_4, R1.Pin_0
  N3: S2.Pin_3, S2.Pin_4, R2.Pin_0
  N4: S3.Pin_3, S3.Pin_4, R3.Pin_0
  N5: S4.Pin_3, S4.Pin_4, R4.Pin_0
  GND: R1.Pin_1, U2.E, R2.Pin_1, R3.Pin_1, R4.Pin_1, R12.Pin_0, U4.VSS, U4.R_W, U4.DB0, U4.DB1, U4.DB2, U4.DB3, part.GND, part_3.GND, R17.Pin_0, U1.GND, R20.Pin_0, R21.Pin_0, R22.Pin_0, R23.Pin_0, R24.Pin_0, R25.Pin_0
  N6: U2.S, U4.VO
  VCC: U2.A, U4.VDD, U4.A, part.VCC, part_3.VCC, U1.5V
  N7: R5.Pin_1, DI1.cathodeD
  N8: R12.Pin_1, U4.K
  N9: U4.DB7, R20.Pin_1
  N10: DI1.cathodeE, R16.Pin_1
  N11: DI1.cathodeC, R8.Pin_1
  N12: DI1.cathodeB, R15.Pin_1
  N13: DI1.cathodeA, R14.Pin_1
  N14: DI1.cathodeF, DI1.cathodeG, R13.Pin_1
  N15: part.SIG, R19.Pin_1
  N16: part_2.SIG, R18.Pin_1
  N17: part_3.SIG, R17.Pin_1

custom parts:
  TTP223B Capacitive Touch Sensor Module: The TTP223B capacitive touch sensor module uses the TTP223B IC. The appropriate voltage is approximately 2 to 5.5 volts.
  Carte NUCLEO H755ZI-Q: Carte prototype double coeurs ARM
